// Logisim project seq_circuit.circ as structural Verilog: 1 circuit, main circuit main
module main (
  input  X,
  input  Y,
  output S
);

  wire and_1_out, and_2_out, clock_out, D_q, or_1_out, xor_1_out;

  xor xor_1 (xor_1_out, X, Y);
  and and_1 (and_1_out, X, Y);
  Clock clock (.out(clock_out));
  D_Flip_Flop D (.clk(clock_out), .D(or_1_out), .Q(D_q));  // open: Qn, preset, en, reset
  xor xor_2 (S, xor_1_out, D_q);
  and and_2 (and_2_out, xor_1_out, D_q);
  or or_1 (or_1_out, and_2_out, and_1_out);

  // Notes on the sheet:
  //   C
endmodule
